# Fritzing sketch Fritzing_file (saved by Fritzing 0.9.3b)
breadboards: 1

parts:
  Part1 = Arduino Uno (Rev3)
  Keypad4x1 = Keypad Membran 4x4
  LED1 = smd LED [color="Red (633nm)" package="1206 [SMD]"]
  LED2 = smd LED [color="Green (570nm)" package="1206 [SMD]"]
  R1 = Resistor [tolerance=±5% resistance=220 package="2512 [SMD]"]
  R2 = Resistor [tolerance=±5% resistance=220 package="2512 [SMD]"]
  J1 = Piezo Speaker
  KY-1 = Keyes Relay [package=THT]
  M1 = DC Motor

nets:
  N1: Part1.D8, Keypad4x1.Pin2
  N2: Part1.D9_PWM, Keypad4x1.Pin1
  N3: Part1.D11_PWM/MOSI, KY-1.signal
  N4: Part1.D12/MISO, J1.pin2
  N5: Part1.D13/SCK, LED1.cathode, LED2.anode, R2.Pin_1
  N6: Part1.GND, LED2.cathode, J1.pin1, KY-1.ground, KY-1.C
  N7: Part1.D2, Keypad4x1.Pin8
  N8: Part1.D3_PWM, Keypad4x1.Pin7
  N9: Part1.D4, Keypad4x1.Pin6
  N10: Part1.D5_PWM, Keypad4x1.Pin5
  N11: Part1.D6_PWM, Keypad4x1.Pin4
  N12: Part1.D7, Keypad4x1.Pin3
  N13: Part1.5V, R1.Pin_1, KY-1.power
  N14: KY-1.NO, M1.pin_1

notes:
  Use Dc Power Supply of 5v

custom parts:
  Keypad Membran 4x4: Membrane Keypad 4x4 Matrix
  Keyes Relay: The Keyes 5V relay module is suitable for SCM development, home appliance control. It uses a 5V~12V TIL control signal which can control DC / AC signal.
